// Logisim project correction.circ as structural Verilog: 1 circuit, main circuit main
module main (
  input  A,
  input  in_2,
  input  in_3,
  output out_4
);

  wire and_1_out, and_2_out, or_1_out;

  or or_1 (or_1_out, in_2, in_3);
  and and_1 (and_1_out, A, A, or_1_out);
  and and_2 (and_2_out, in_2, in_2, in_3);
  or or_2 (out_4, and_1_out, and_1_out, and_2_out, and_2_out);

  // Notes on the sheet:
  //   B
  //   C
endmodule
